# Fritzing sketch Wiring (saved by Fritzing 0.9.3b)
breadboards: 1

parts:
  Raspberry_Pi_2 = Raspberry Pi 3 [part_number=RPI-3-V1.2]
  CC1101_Transceiver = Header 5x2 [package=2x5-ra]
  Bauteil1 = Arduino Nano (Rev3.0) (ICSP)

nets:
  N1: Raspberry_Pi_2.GPIO2, Bauteil1.A4
  N2: Raspberry_Pi_2.GPIO3, Bauteil1.A5
  GND: Raspberry_Pi_2.GND, CC1101_Transceiver.9, Bauteil1.GND
  5V: Raspberry_Pi_2.5V, Bauteil1.VIN
  N3: CC1101_Transceiver.1, Bauteil1.3V3
  N4: CC1101_Transceiver.3, Bauteil1.D13/SCK
  N5: CC1101_Transceiver.4, Bauteil1.D11/MOSI
  N6: CC1101_Transceiver.5, Bauteil1.D9
  N7: CC1101_Transceiver.6, Bauteil1.D12/MISO
  N8: CC1101_Transceiver.7, Bauteil1.D2
  N9: CC1101_Transceiver.8, Bauteil1.D10
